# Fritzing sketch Breadboard (saved by Fritzing 0.9.1b)
breadboards: 1

parts:
  Part1 = Arduino Uno (Rev3)
  R1 = Resistor [tolerance=±5% resistance=10k package=THT]
  R2 = Photocell (LDR) [package=THT]
  RHT1 = Humidity and Temperature Sensor RHT03 [part_number=DHT11]

nets:
  N1: Part1.A0, R1.Pin_1, R2.pin_1
  N2: Part1.D7, RHT1.Data-signal
  N3: Part1.5V, R2.pin_0, RHT1.GND_1
  N4: Part1.GND, R1.Pin_0, RHT1.GND_2

notes:
  DHT 11 Can have different Pin setup depending on if you are using a "shield" or a bare (which needs a resistor)
  Bill of materials:
  DHT 11
  10k Resistor
  LDR
